# Fritzing sketch feather_MCP9808 (saved by Fritzing 0.9.9b)
breadboards: 1

parts:
  Part2 = Adafruit Feather HUZZAH ESP8266 [part_number="Adafruit #2821"]
  ZS-042_RTC1 = ZS-042 RTC Module  # not connected
  Part3 = MCP9808 High Accuracy I2C Temperature Sensor [part_number=1782]

nets:
  GND: Part2.GND, Part3.GND
  3.3V: Part2.3.3V, Part3.VDD
  N1: Part2.GPIO5/SCL, Part3.SCL
  N2: Part2.GPIO4/SDA, Part3.SDA

custom parts:
  Adafruit Feather HUZZAH ESP8266: his is the Adafruit Feather HUZZAH ESP8266 - our take on an 'all-in-one' ESP8266 WiFi development board with built in USB and battery charging. Its an ESP8266 WiFi module with all the extras you need, ready to rock! We have other boards in the Feather family, check'em out here. At the Feather HUZZAH's heart is an ESP8266 WiFi microcontroller clocked at 80 MHz and at 3.3V logic. This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
  MCP9808 High Accuracy I2C Temperature Sensor: This I2C digital temperature sensor is one of the more accurate/precise we've ever seen, with a typical accuracy of ±0.25°C over the sensor's -40°C to +125°C range and precision of +0.0625°C. They work great with any microcontroller using standard i2c. There are 3 address pins so you can connect up to 8 to a single I2C bus without address collisions. Best of all, a wide voltage range makes is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
