# Fritzing sketch feather_sdcard2 (saved by Fritzing 0.9.9b)
breadboards: 1

parts:
  Part2 = Adafruit Feather HUZZAH ESP8266 [part_number="Adafruit #2821"]
  microSD_Transflash2 = SparkFun - microSD Transflash

nets:
  N1: Part2.GPIO12/MISO, microSD_Transflash2.DO
  N2: Part2.GPIO13/MOSI, microSD_Transflash2.DI
  N3: Part2.GPIO14/SCK, microSD_Transflash2.SCK
  GND: Part2.GND, microSD_Transflash2.GND
  3.3V: Part2.3.3V, microSD_Transflash2.VCC
  N4: Part2.GPIO0, microSD_Transflash2.CS

custom parts:
  Adafruit Feather HUZZAH ESP8266: his is the Adafruit Feather HUZZAH ESP8266 - our take on an 'all-in-one' ESP8266 WiFi development board with built in USB and battery charging. Its an ESP8266 WiFi module with all the extras you need, ready to rock! We have other boards in the Feather family, check'em out here. At the Feather HUZZAH's heart is an ESP8266 WiFi microcontroller clocked at 80 MHz and at 3.3V logic. This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
