# Fritzing sketch feather_switch (saved by Fritzing 0.9.4)
breadboards: 1

parts:
  Switch = Pushbutton [package="[SMD]"]
  Part2 = Adafruit Feather HUZZAH ESP8266 [part_number="Adafruit #2821"]
  Relay = mystery part, 4 pins [chip_label=SSR]
  Resistor = Resistor [tolerance=±5% resistance=100 package=THT]
  LED = LED - 5mm [color="Blue (430nm)" package="5 mm [THT]"]

nets:
  N1: Switch.Pin_1, Switch.Pin_2, Part2.GND, Relay.pin2
  N2: Switch.Pin_3, Switch.Pin_4, Part2.GPIO2
  N3: Part2.GPIO14/SCK, Relay.pin1
  N4: Part2.3.3V, LED.anode
  N5: Relay.pin4, Resistor.Pin_0
  N6: Resistor.Pin_1, LED.cathode

custom parts:
  Adafruit Feather HUZZAH ESP8266: his is the Adafruit Feather HUZZAH ESP8266 - our take on an 'all-in-one' ESP8266 WiFi development board with built in USB and battery charging. Its an ESP8266 WiFi module with all the extras you need, ready to rock! We have other boards in the Feather family, check'em out here. At the Feather HUZZAH's heart is an ESP8266 WiFi microcontroller clocked at 80 MHz and at 3.3V logic. This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
