# Fritzing sketch feather_thermistor (saved by Fritzing 0.9.4)
breadboards: 1

parts:
  Part2 = Adafruit Feather HUZZAH ESP8266 [part_number="Adafruit #2821"]
  R1 = Resistor [tolerance=±5% resistance=100k package="2512 [SMD]"]
  R3 = Temperature Sensor (Thermistor) [thermistor_type=NTC package=THT]

nets:
  N1: Part2.ADC, R1.Pin_0, R3.pin_1
  N2: Part2.GND, R3.pin_0
  N3: Part2.3.3V, R1.Pin_1

notes:
  R1
  Vdata
  3V3
  GND
  RTH2

custom parts:
  Adafruit Feather HUZZAH ESP8266: his is the Adafruit Feather HUZZAH ESP8266 - our take on an 'all-in-one' ESP8266 WiFi development board with built in USB and battery charging. Its an ESP8266 WiFi module with all the extras you need, ready to rock! We have other boards in the Feather family, check'em out here. At the Feather HUZZAH's heart is an ESP8266 WiFi microcontroller clocked at 80 MHz and at 3.3V logic. This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
