# Fritzing sketch feather_tsl237module1 (saved by Fritzing 0.9.4)
breadboards: 1

parts:
  Part2 = Adafruit Feather HUZZAH ESP8266 [part_number="Adafruit #2821"]
  LED2 = DUO LED RG [package="5 mm [THT]"]

nets:
  GND: Part2.GND, LED2.GND
  3.3V: Part2.3.3V, LED2.Vin
  N1: Part2.GPIO4/SDA, LED2.Vout

notes:
  GND
  Vout
  Vin
  TSL237
  Divider/counter

custom parts:
  Adafruit Feather HUZZAH ESP8266: his is the Adafruit Feather HUZZAH ESP8266 - our take on an 'all-in-one' ESP8266 WiFi development board with built in USB and battery charging. Its an ESP8266 WiFi module with all the extras you need, ready to rock! We have other boards in the Feather family, check'em out here. At the Feather HUZZAH's heart is an ESP8266 WiFi microcontroller clocked at 80 MHz and at 3.3V logic. This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
  DUO LED RG: A 5mm DUO-color LED with red and green inside. Pin order: red - com. cathode - green
