# Fritzing sketch feather_voltage_divider2 (saved by Fritzing 0.9.4)
breadboards: 1

parts:
  Part2 = Adafruit Feather HUZZAH ESP8266 [part_number="Adafruit #2821"]
  BAT1 = 18650 battery holder [package=battery-18650-kit]
  R2 = Resistor [tolerance=±5% resistance=100 package="2512 [SMD]"]
  R1 = Resistor [tolerance=±5% resistance=470 package="2512 [SMD]"]

nets:
  N1: Part2.ADC, R2.Pin_1, R1.Pin_0
  N2: Part2.GND, BAT1.-, R2.Pin_0
  N3: BAT1.+, R1.Pin_1

notes:
  R2
  R1
  Vdata
  Vin
  GND

custom parts:
  Adafruit Feather HUZZAH ESP8266: his is the Adafruit Feather HUZZAH ESP8266 - our take on an 'all-in-one' ESP8266 WiFi development board with built in USB and battery charging. Its an ESP8266 WiFi module with all the extras you need, ready to rock! We have other boards in the Feather family, check'em out here. At the Feather HUZZAH's heart is an ESP8266 WiFi microcontroller clocked at 80 MHz and at 3.3V logic. This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
  18650 battery holder: 18650 Battery Holder
